// Logisim project Assignment2.circ as structural Verilog: 8 circuits, main circuit HalfAdder
module Mux4Way16 (
  input  [1:0] sel,
  input  [15:0] a,
  input  [15:0] b,
  input  [15:0] c,
  input  [15:0] d,
  output [15:0] out
);

  wire [15:0] multiplexer_1_out, multiplexer_2_out;

  Multiplexer #(.enable("false"), .width(16)) multiplexer_1 (.in0(a), .in1(b), .out(multiplexer_1_out), .sel(sel[0]));
  Multiplexer #(.enable("false"), .width(16)) multiplexer_2 (.in0(c), .in1(d), .out(multiplexer_2_out), .sel(sel[0]));
  Multiplexer #(.enable("false"), .width(16)) multiplexer_3 (
    .in0(multiplexer_1_out), .in1(multiplexer_2_out), .out(out), .sel(sel[1]));

  // Notes on the sheet:
  //   Function:
  //   If sel == 00, out = a
  //   If sel == 01, out = b
  //   If sel == 10, out = c
  //   If sel == 11, out = d
  //   You can build this out of three Mux16 gates (you can use built-in). 
  //   You will need to split the selection bits up. Then, think about how to use those components 
  //   to select between 4 possible inputs.
endmodule

module Mux8Way16 (
  input  [2:0] sel,
  input  [15:0] a,
  input  [15:0] b,
  input  [15:0] c,
  input  [15:0] d,
  input  [15:0] e,
  input  [15:0] f,
  input  [15:0] g,
  input  [15:0] h,
  output [15:0] out
);

  wire [15:0] mux4way16_1_out, mux4way16_2_out;

  Mux4Way16 mux4way16_1 (.sel(sel[1:0]), .a(a), .b(b), .c(c), .d(d), .out(mux4way16_1_out));
  Mux4Way16 mux4way16_2 (.sel(sel[1:0]), .a(e), .b(f), .c(g), .d(h), .out(mux4way16_2_out));
  Multiplexer #(.enable("false"), .width(16)) multiplexer_1 (
    .in0(mux4way16_1_out), .in1(mux4way16_2_out), .out(out), .sel(sel[2]));

  // Notes on the sheet:
  //   Function:
  //   If sel == 000, out = a
  //   If sel == 001, out = b
  //   If sel == 010, out = c
  //   If sel == 011, out = d
  //   If sel == 100, out = e
  //   If sel == 101, out = f
  //   If sel == 110, out = g
  //   If sel == 111, out = h
  //   Take a recursive approach here. Use Mux4Way16 circuits here.
endmodule

module DMux4Way (
  input  [1:0] sel,
  input  in,
  output a,
  output b,
  output c,
  output d
);

  wire demultiplexer_1_out0, demultiplexer_1_out1;

  Demultiplexer #(.enable("false")) demultiplexer_1 (
    .out0(demultiplexer_1_out0), .out1(demultiplexer_1_out1), .in(in), .sel(sel[1]));
  Demultiplexer #(.enable("false")) demultiplexer_2 (.out0(a), .out1(b), .in(demultiplexer_1_out0), .sel(sel[0]));
  Demultiplexer #(.enable("false")) demultiplexer_3 (.out0(c), .out1(d), .in(demultiplexer_1_out1), .sel(sel[0]));

  // Notes on the sheet:
  //   Function:
  //   If sel == 00, [a, b, c, d] = [in, 0, 0, 0]
  //   If sel == 01, [a, b, c, d] = [0, in, 0, 0]
  //   If sel == 10, [a, b, c, d] = [0, 0, in, 0]
  //   If sel == 11, [a, b, c, d] = [0, 0, 0, in]
  //   Same advice as for the Mux4Way16 gate (but for DMux).
endmodule

module DMux8Way (
  input  [2:0] sel,
  input  in,
  output a,
  output b,
  output c,
  output d,
  output e,
  output f,
  output g,
  output h
);

  wire demultiplexer_1_out0, demultiplexer_1_out1;

  Demultiplexer #(.enable("false")) demultiplexer_1 (
    .out0(demultiplexer_1_out0), .out1(demultiplexer_1_out1), .in(in), .sel(sel[2]));
  DMux4Way dmux4way_1 (.sel(sel[1:0]), .in(demultiplexer_1_out0), .a(a), .b(b), .c(c), .d(d));
  DMux4Way dmux4way_2 (.sel(sel[1:0]), .in(demultiplexer_1_out1), .a(e), .b(f), .c(g), .d(h));

  // Notes on the sheet:
  //   Function:
  //   [a, b, c, d, e, f, g, h] = 
  //   								[in, 0, 0, 0, 0, 0, 0, 0] if sel == 000
  //   								[0, in, 0, 0, 0, 0, 0, 0] if sel == 001
  //   								[0, 0, in, 0, 0, 0, 0, 0] if sel == 010
  //   								[0, 0, 0, in, 0, 0, 0, 0] if sel == 011
  //   								[0, 0, 0, 0, in, 0, 0, 0] if sel == 100
  //   								[0, 0, 0, 0, 0, in, 0, 0] if sel == 101
  //   								[0, 0, 0, 0, 0, 0, in, 0] if sel == 110
  //   								[0, 0, 0, 0, 0, 0, 0, in] if sel == 111
  //   Same advice as for the Mux8Way16 gate (but for DMux)
endmodule

module HalfAdder (
  input  a,
  input  b,
  output sum,
  output carry
);

  xor xor_1 (sum, a, b);
  and and_1 (carry, b, a);

  // Notes on the sheet:
  //   Function:
  //   sum = right bit/LSB of a + b
  //   carry = left bit/MSB of a + b
  //   Building a truth table should lead to a trivial solution
endmodule

module FullAdder (
  input  a,
  input  b,
  input  c,
  output carry,
  output sum
);

  wire halfadder_1_carry, halfadder_1_sum, halfadder_2_carry;

  HalfAdder halfadder_1 (.a(a), .b(b), .sum(halfadder_1_sum), .carry(halfadder_1_carry));
  or or_1 (carry, halfadder_1_carry, halfadder_2_carry);
  HalfAdder halfadder_2 (.a(c), .b(halfadder_1_sum), .sum(sum), .carry(halfadder_2_carry));

  // Notes on the sheet:
  //   Function:
  //   Sum = right bit of a + b + c
  //   Carry = left bit of a + b + c
  //   This circuit can be implemented using two half adders
  //   and one additional gate
endmodule

module Add16 (
  input  c,
  input  [15:0] a,
  input  [15:0] b,
  output [15:0] out,
  output carry
);

  wire fulladder_1_carry, fulladder_2_carry, fulladder_3_carry, fulladder_4_carry, fulladder_5_carry,
       fulladder_6_carry, fulladder_7_carry, fulladder_8_carry, fulladder_9_carry, fulladder_10_carry,
       fulladder_11_carry, fulladder_12_carry, fulladder_13_carry, fulladder_14_carry, fulladder_15_carry;

  FullAdder fulladder_1 (.a(a[0]), .b(b[0]), .c(c), .sum(out[0]), .carry(fulladder_1_carry));
  FullAdder fulladder_2 (.a(a[1]), .b(b[1]), .c(fulladder_1_carry), .sum(out[1]), .carry(fulladder_2_carry));
  FullAdder fulladder_3 (.a(a[2]), .b(b[2]), .c(fulladder_2_carry), .sum(out[2]), .carry(fulladder_3_carry));
  FullAdder fulladder_4 (.a(a[3]), .b(b[3]), .c(fulladder_3_carry), .sum(out[3]), .carry(fulladder_4_carry));
  FullAdder fulladder_5 (.a(a[4]), .b(b[4]), .c(fulladder_4_carry), .sum(out[4]), .carry(fulladder_5_carry));
  FullAdder fulladder_6 (.a(a[5]), .b(b[5]), .c(fulladder_5_carry), .sum(out[5]), .carry(fulladder_6_carry));
  FullAdder fulladder_7 (.a(a[6]), .b(b[6]), .c(fulladder_6_carry), .sum(out[6]), .carry(fulladder_7_carry));
  FullAdder fulladder_8 (.a(a[7]), .b(b[7]), .c(fulladder_7_carry), .sum(out[7]), .carry(fulladder_8_carry));
  FullAdder fulladder_9 (.a(a[8]), .b(b[8]), .c(fulladder_8_carry), .sum(out[8]), .carry(fulladder_9_carry));
  FullAdder fulladder_10 (.a(a[9]), .b(b[9]), .c(fulladder_9_carry), .sum(out[9]), .carry(fulladder_10_carry));
  FullAdder fulladder_11 (.a(a[10]), .b(b[10]), .c(fulladder_10_carry), .sum(out[10]), .carry(fulladder_11_carry));
  FullAdder fulladder_12 (.a(a[11]), .b(b[11]), .c(fulladder_11_carry), .sum(out[11]), .carry(fulladder_12_carry));
  FullAdder fulladder_13 (.a(a[12]), .b(b[12]), .c(fulladder_12_carry), .sum(out[12]), .carry(fulladder_13_carry));
  FullAdder fulladder_14 (.a(a[13]), .b(b[13]), .c(fulladder_13_carry), .sum(out[13]), .carry(fulladder_14_carry));
  FullAdder fulladder_15 (.a(a[14]), .b(b[14]), .c(fulladder_14_carry), .sum(out[14]), .carry(fulladder_15_carry));
  FullAdder fulladder_16 (.a(a[15]), .b(b[15]), .c(fulladder_15_carry), .sum(out[15]), .carry(carry));

  // Notes on the sheet:
  //   Function:
  //   out = a + b + c (only 1 bit)
  //   The addition of two signed numbers can be done bit-wise, from right to left.
  //   In step 0, the least significant pair of bits is added, and the carry bit is fed into
  //   the addition of the next significant pair of bits. The process continues until in step
  //   n - 1, the most significant pair of bits is added. Note that each step involves
  //   the addition of three bits.
  //   The carry output should indicate whether there is a carry over from the last bit
endmodule

module Inc16 (
  input  [15:0] in,
  output [15:0] out,
  output out_3
);

  Add16 add16_1 (.a(in), .b(16'h1), .out(out), .carry(out_3));  // open: c

  // Notes on the sheet:
  //   16-bit incrementer.
  //   out = in + 1
  //   Use a constant (Wiring>Constant) for this
endmodule
